# Fritzing sketch usb (saved by Fritzing 0.9.6b)
breadboards: 1

parts:
  Part1 = Arduino Uno (Rev3) - ICSP
  X1 = USB Connectors [package=usb-b-smt]
  R1 = Resistor [tolerance=±5% power=0.25 resistance=1k package=THT]
  R2 = Resistor [tolerance=±5% power=0.25 resistance=560 package=THT]
  Q2 = Basic FET N-Channel [package="TO220 [THT]"]
  Q1 = Basic FET N-Channel [package="TO220 [THT]"]

nets:
  N1: Part1.5V, Q2.gate, Q1.gate
  N2: Part1.D2, Q1.drain
  N3: Part1.D4, Q2.drain
  N4: Part1.3V3, R1.Pin_1
  GND: Part1.GND, X1.GND
  N5: X1.D+, Q1.source
  N6: X1.D-, R2.Pin_0, Q2.source
  N7: R1.Pin_0, R2.Pin_1
